// Logisim project control_logic.circ as structural Verilog: 1 circuit, main circuit control_logic
module control_logic (
  input  [31:0] inst,
  input  BrEq,
  input  BrLt,
  output PCSel,
  output RegWEn,
  output [2:0] ImmSel,
  output BrUn,
  output ASel,
  output BSel,
  output [3:0] ALUSel,
  output MemRW,
  output [1:0] WBSel
);

  wire func3_R_is_0, func7_R_is_0, is_add, is_R_format;
  wire [2:0] func3_R;
  wire [6:0] func7_R;
  wire [24:0] demultiplexer_1_out1;

  Comparator #(.width(7), .mode("unsigned")) comparator_1 (
    .a(inst[6:0]), .b(7'b0110011), .eq(is_R_format));  // open: gt, lt
  Demultiplexer #(.width(32), .enable("false")) demultiplexer_1 (
    .out1({func7_R, demultiplexer_1_out1[24:15], func3_R, demultiplexer_1_out1[11:0]}), .in(inst),
    .sel(is_R_format));  // open: out0
  Comparator #(.width(3), .mode("unsigned")) comparator_2 (.a(func3_R), .b(3'b000), .eq(func3_R_is_0));  // open: gt, lt
  Comparator #(.width(7), .mode("unsigned")) comparator_3 (
    .a(func7_R), .b({7{1'b0}}), .eq(func7_R_is_0));  // open: gt, lt
  and and_1 (is_add, func3_R_is_0, func7_R_is_0);
  Multiplexer #(.enable("false")) multiplexer_1 (.in1(1'b0), .out(PCSel), .sel(is_add));  // open: in0
  Multiplexer #(.enable("false")) multiplexer_2 (.in1(1'b1), .out(RegWEn), .sel(is_add));  // open: in0
  Multiplexer #(.enable("false")) multiplexer_3 (.in1(1'b0), .out(ASel), .sel(is_add));  // open: in0
  Multiplexer #(.enable("false")) multiplexer_4 (.in1(1'b0), .out(BSel), .sel(is_add));  // open: in0
  Multiplexer #(.width(4), .enable("false")) multiplexer_5 (.in1(4'b0000), .out(ALUSel), .sel(is_add));  // open: in0
  Multiplexer #(.width(2), .enable("false")) multiplexer_6 (.in1(2'b01), .out(WBSel), .sel(is_add));  // open: in0

  // Other names for the same wires on the sheet: opcode[6:0] = inst[6:0]

  // Notes on the sheet:
  //   INPUTS to your circuit
  //   DON'T CHANGE THE LOCATIONS OF THE INPUTS AND OUTPUTS!
  //   OUTPUT from your circuit
endmodule
